# Fritzing sketch OSCHSSP_electrical_design_surculus_v1.0 (saved by Fritzing 1.0.1rc)
perfboards: 1

parts:
  J1 = female pin header, 15 pins [form="♀ (female)"]
  J3 = female pin header, 6 pins [form="♀ (female)"]
  J4 = female pin header, 6 pins [form="♀ (female)"]
  Part1 = Arduino Nano (Rev3.0)
  J2 = female pin header, 15 pins [form="♀ (female)"]
  J5 = female pin header, 4 pins [form="♀ (female)"]
  J6 = female pin header, 15 pins [form="♀ (female)"]
  J7 = female pin header, 15 pins [form="♀ (female)"]
  J8 = Camdenboss CTB0158-2 [part_number=CTB0158-2 package=THT]

nets:
  N1: J1.pin1, Part1.D13/SCK, J7.pin1
  N2: J1.pin2, Part1.3V3, J5.pin2, J7.pin2
  N3: J1.pin3, Part1.AREF, J7.pin3
  N4: J1.pin4, Part1.A0, J7.pin4
  N5: J1.pin5, Part1.A1, J7.pin5
  N6: J1.pin6, Part1.A2, J7.pin6
  N7: J1.pin7, Part1.A3, J7.pin7
  N8: J1.pin8, Part1.A4, J5.pin3, J7.pin8
  N9: J1.pin9, Part1.A5, J5.pin4, J7.pin9
  N10: J1.pin10, Part1.A6, J7.pin10
  N11: J1.pin11, Part1.A7, J7.pin11
  N12: J1.pin12, J3.pin6, J4.pin1, Part1.5V
  N13: J1.pin13, Part1.RESET, J2.pin13
  N14: J1.pin14, J3.pin4, Part1.GND, J2.pin12, J5.pin1, J6.pin12, J6.pin13, J6.pin14, J7.pin14, J8.pin1
  N15: J1.pin15, Part1.VIN, J8.pin2
  N16: J3.pin1, J4.pin6, Part1.D6, J2.pin7, J6.pin7
  N17: J3.pin2, Part1.D7, J2.pin6, J6.pin6
  N18: J3.pin3, J4.pin4, Part1.D8, J2.pin5, J6.pin5
  N19: J4.pin3, J6.pin15
  N20: J4.pin5, Part1.D5, J2.pin8, J6.pin8
  N21: Part1.D1/TX, J2.pin15
  N22: Part1.D0/RX, J2.pin14
  N23: Part1.D2, J2.pin11
  N24: Part1.D3, J2.pin10, J6.pin10
  N25: Part1.D4, J2.pin9, J6.pin9
  N26: Part1.D9, J2.pin4, J6.pin4
  N27: Part1.D10, J2.pin3, J6.pin3
  N28: Part1.D11/MOSI, J2.pin2, J6.pin2
  N29: Part1.D12/MISO, J2.pin1, J6.pin1
