# Fritzing sketch OSCHSSP_electrical_design_surculus_v1.0 (saved by Fritzing 1.0.1rc)
perfboards: 1

parts:
  J1 = female pin header, 15 pins [form="♀ (female)"]
  J2 = female pin header, 15 pins [form="♀ (female)"]
  J3 = female pin header, 6 pins [form="♀ (female)"]  # not connected
  J4 = female pin header, 6 pins [form="♀ (female)"]  # not connected
  J5 = female pin header, 4 pins [form="♀ (female)"]  # not connected
  Part1 = Arduino Nano (Rev3.0)

nets:
  N1: J1.pin1, Part1.D13/SCK
  N2: J1.pin2, Part1.3V3
  N3: J1.pin3, Part1.AREF
  N4: J1.pin4, Part1.A0
  N5: J1.pin5, Part1.A1
  N6: J1.pin6, Part1.A2
  N7: J1.pin7, Part1.A3
  N8: J1.pin8, Part1.A4
  N9: J1.pin9, Part1.A5
  N10: J1.pin10, Part1.A6
  N11: J1.pin11, Part1.A7
  N12: J1.pin12, Part1.5V
  N13: J1.pin13, J2.pin13, Part1.RESET
  N14: J1.pin14, J2.pin12, Part1.GND
  N15: J1.pin15, Part1.VIN
  N16: J2.pin1, Part1.D12/MISO
  N17: J2.pin2, Part1.D11/MOSI
  N18: J2.pin3, Part1.D10
  N19: J2.pin4, Part1.D9
  N20: J2.pin5, Part1.D8
  N21: J2.pin6, Part1.D7
  N22: J2.pin7, Part1.D6
  N23: J2.pin8, Part1.D5
  N24: J2.pin9, Part1.D4
  N25: J2.pin10, Part1.D3
  N26: J2.pin11, Part1.D2
  N27: J2.pin14, Part1.D0/RX
  N28: J2.pin15, Part1.D1/TX
